# Fritzing sketch ArduinoModule (saved by Fritzing 0.9.4)
breadboards: 1

parts:
  NRF24L1 = NRF24L01
  Componente1 = Arduino Uno (Rev3) - ICSP
  C1 = Electrolytic Capacitor [capacitance=1µF package="100 mil [THT, electrolytic]"]
  IR1 = TSOP312.., 314.. [package=THT]

nets:
  VCC: NRF24L1.VCC, Componente1.3V3, C1.+, IR1.Data
  N1: NRF24L1.CSN, Componente1.D10_PWM/SS
  N2: NRF24L1.MOSI, Componente1.D11_PWM/MOSI
  GND: NRF24L1.GND, Componente1.GND, C1.-, IR1.Vs
  N3: NRF24L1.CE, Componente1.D9_PWM
  N4: NRF24L1.SCK, Componente1.D13/SCK
  N5: NRF24L1.MISO, Componente1.ICSP_MISO, Componente1.D12/MISO
  N6: Componente1.D4, IR1.GND

notes:
  GND = Black
  VCC = Red
  CE = Yellow
  CSN = Green
  SCK = Orange
  MOSI = White
  MISO = Brown
  IRQ = Not Connected

custom parts:
  NRF24L01: NRF24L01 module
